# Fritzing sketch 2-control-LED-with-button (saved by Fritzing 0.9.3b)
breadboards: 1

parts:
  Raspberry_Pi_1 = Raspberry Pi 3 [part_number=RPI-3-V1.2]
  LED1 = LED - 3mm [color="Red (633nm)" package="3 mm [THT]"]
  R1 = Resistor [tolerance=±5% resistance=220 package="0603 [SMD]"]
  S1 = Round Pushbutton

nets:
  N1: Raspberry_Pi_1.GIPO19, S1.leg1
  N2: Raspberry_Pi_1.GIPO26, LED1.anode
  N3: Raspberry_Pi_1.GND, R1.Pin_0
  N4: Raspberry_Pi_1.5V, S1.leg0
  N5: LED1.cathode, R1.Pin_1
