# Fritzing sketch 3-PWM (saved by Fritzing 0.9.3b)
breadboards: 1

parts:
  Raspberry_Pi_1 = Raspberry Pi 3 [part_number=RPI-3-V1.2]
  LED1 = LED - 5mm [color="Red (633nm)" package="5 mm [THT]"]
  R1 = Resistor [tolerance=±5% resistance=220 package=THT]

nets:
  N1: Raspberry_Pi_1.GIPO18, R1.Pin_1
  N2: Raspberry_Pi_1.GND, LED1.cathode
  N3: LED1.anode, R1.Pin_0
